// Logisim project 2bit_synchronous_counter .circ as structural Verilog: 1 circuit, main circuit main
module main (
  output out_1,
  output out_2
);

  wire clock_1_out, not_1_out, xor_1_out;

  Clock clock_1 (.out(clock_1_out));
  D_Flip_Flop q1 (.D(xor_1_out), .clk(clock_1_out), .Q(out_1));  // open: Qn, preset, reset
  D_Flip_Flop q0 (.D(not_1_out), .clk(clock_1_out), .Q(out_2));  // open: Qn, preset, reset
  not not_1 (not_1_out, out_2);
  xor xor_1 (xor_1_out, out_1, out_2);
endmodule
