// Logisim project 2bit_synchronous_counter_with_enable_and_reset.circ as structural Verilog: 1 circuit, main circuit main
module main (
  input  in_1,
  input  enable,
  input  R,
  input  in_4,
  output out_5,
  output out_6
);

  wire clock_1_out, multiplexer_1_out, multiplexer_2_out, multiplexer_3_out, multiplexer_4_out, not_1_out,
       xor_1_out;

  Multiplexer multiplexer_1 (.in0(multiplexer_4_out), .in1(in_1), .out(multiplexer_1_out), .sel(R));
  Clock clock_1 (.out(clock_1_out));
  Multiplexer multiplexer_2 (.in0(multiplexer_3_out), .in1(in_4), .out(multiplexer_2_out), .sel(R));
  D_Flip_Flop q1 (.D(multiplexer_1_out), .clk(clock_1_out), .Q(out_5));  // open: Qn, preset, reset
  D_Flip_Flop q0 (.D(multiplexer_2_out), .clk(clock_1_out), .Q(out_6));  // open: Qn, preset, reset
  not not_1 (not_1_out, out_6);
  Multiplexer multiplexer_3 (.in0(out_6), .in1(not_1_out), .out(multiplexer_3_out), .sel(enable));
  Multiplexer multiplexer_4 (.in0(out_5), .in1(xor_1_out), .out(multiplexer_4_out), .sel(enable));
  xor xor_1 (xor_1_out, out_5, out_6);
endmodule
