// Logisim project 4bit_counter_with_HEX_display.circ as structural Verilog: 1 circuit, main circuit main
module main (
  output out_1,
  output out_2,
  output out_3,
  output out_4
);

  wire and_1_out, and_2_out, CLK_out, not_1_out, xor_1_out, xor_2_out, xor_3_out;

  Clock CLK (.out(CLK_out));
  D_Flip_Flop q3 (.D(xor_3_out), .clk(CLK_out), .Q(out_1));  // open: Qn, preset, reset
  D_Flip_Flop q2 (.D(xor_2_out), .clk(CLK_out), .Q(out_2));  // open: Qn, preset, reset
  D_Flip_Flop q1 (.D(xor_1_out), .clk(CLK_out), .Q(out_3));  // open: Qn, preset, reset
  D_Flip_Flop q0 (.D(not_1_out), .clk(CLK_out), .Q(out_4));  // open: Qn, preset, reset
  not not_1 (not_1_out, out_4);
  xor xor_1 (xor_1_out, out_3, out_4);
  xor xor_2 (xor_2_out, out_2, and_1_out);
  and and_1 (and_1_out, out_3, out_4);
  xor xor_3 (xor_3_out, out_1, and_2_out);
  and and_2 (and_2_out, out_2, and_1_out);
  Hex_Digit_Display hex_digit_display_1 (.value({out_1, out_2, out_3, out_4}));  // open: dp
endmodule
