// Logisim project SR_lanch.circ as structural Verilog: 1 circuit, main circuit main
module main (
  input  A,
  input  B,
  output out_3,
  output out_4
);

  nand nand_1 (out_3, A, out_4);
  nand nand_2 (out_4, out_3, B);
endmodule
