// Logisim project logism_half_adder.circ as structural Verilog: 1 circuit, main circuit main
module main (
  input  cin,
  input  a,
  input  b,
  output sum,
  output carry
);

  wire and_1_out, and_2_out, xor_1_out;

  and and_1 (and_1_out, a, b);
  xor xor_1 (xor_1_out, a, b);
  xor xor_2 (sum, xor_1_out, cin);
  and and_2 (and_2_out, xor_1_out, cin);
  or or_1 (carry, and_2_out, and_1_out);
endmodule
