// Logisim project simplified_circuit.circ as structural Verilog: 1 circuit, main circuit main
module main (
  input  A,
  input  B,
  input  C,
  input  D
);

  wire and_1_out, and_2_out, and_3_out, and_4_out, and_5_out, and_6_out, and_7_out, and_8_out, not_1_out,
       not_2_out, not_3_out, not_4_out, not_5_out, not_6_out, not_7_out, not_8_out, not_9_out, not_10_out,
       not_11_out, not_12_out, not_13_out, not_14_out, not_15_out, or_1_out, or_2_out, xor_1_out;

  not not_1 (not_1_out, A);
  not not_2 (not_2_out, B);
  not not_3 (not_3_out, C);
  not not_4 (not_4_out, D);
  not not_5 (not_5_out, A);
  not not_6 (not_6_out, B);
  not not_7 (not_7_out, D);
  not not_8 (not_8_out, A);
  not not_9 (not_9_out, C);
  not not_10 (not_10_out, B);
  not not_11 (not_11_out, C);
  not not_12 (not_12_out, D);
  not not_13 (not_13_out, B);
  not not_14 (not_14_out, D);
  not not_15 (not_15_out, C);
  and and_1 (and_1_out, not_1_out, not_2_out, not_3_out, not_4_out);
  and and_2 (and_2_out, not_5_out, not_6_out, C, not_7_out);
  and and_3 (and_3_out, not_8_out, B, not_9_out, D);
  and and_4 (and_4_out, A, not_10_out, not_11_out, not_12_out);
  and and_5 (and_5_out, A, not_13_out, C, not_14_out);
  and and_6 (and_6_out, A, B, not_15_out, D);
  and and_7 (and_7_out, not_13_out, not_7_out);
  and and_8 (and_8_out, B, not_9_out, D);
  or or_1 (or_1_out, and_1_out, and_2_out, and_4_out, and_3_out, and_5_out, and_6_out);
  or or_2 (or_2_out, and_7_out, and_8_out);
  LED F_original (.in(or_1_out));
  LED F_simplified (.in(or_2_out));
  xor xor_1 (xor_1_out, or_1_out, or_2_out);
  // RGBLED rgbled_1: pin names not known; wires that end beside it: xor_1_out
endmodule
